# Fritzing sketch RoboticArm (saved by Fritzing 0.9.2b)
circuit board: 21.4541cm x 6.23012cm
breadboards: 2

parts:
  Raspberry_Pi1 = Raspberry Pi 2
  DRV_1 = DRV 8825 Stepper Motor Carrier, High Current [part_number="DRV 8825"]
  DRV_2 = DRV 8825 Stepper Motor Carrier, High Current [part_number="DRV 8825"]
  DRV_3 = DRV 8825 Stepper Motor Carrier, High Current [part_number="DRV 8825"]
  DRV_4 = DRV 8825 Stepper Motor Carrier, High Current [part_number="DRV 8825"]
  DRV_5 = DRV 8825 Stepper Motor Carrier, High Current [part_number="DRV 8825"]
  DRV_6 = DRV 8825 Stepper Motor Carrier, High Current [part_number="DRV 8825"]
  C1 = Electrolytic Capacitor [capacitance=100µF package="200 mil [THT, electrolytic]"]
  C2 = Electrolytic Capacitor [capacitance=100µF package="200 mil [THT, electrolytic]"]
  C3 = Electrolytic Capacitor [capacitance=100µF package="200 mil [THT, electrolytic]"]
  C4 = Electrolytic Capacitor [capacitance=100µF package="200 mil [THT, electrolytic]"]
  C5 = Electrolytic Capacitor [capacitance=100µF package="200 mil [THT, electrolytic]"]
  C6 = Electrolytic Capacitor [capacitance=100µF package="200 mil [THT, electrolytic]"]
  M1 = Stepper Motor - Bipolar
  M2 = Stepper Motor - Bipolar
  M3 = Stepper Motor - Bipolar
  M4 = Stepper Motor - Bipolar
  M5 = Stepper Motor - Bipolar
  M6 = Stepper Motor - Bipolar
  M7 = Stepper Motor - Bipolar
  J1 = Basic Servo
  U1 = DC-DC_CONVERTER [package=dc-dc_converter]
  Power_plug1 = Power plug

nets:
  3V3: Raspberry_Pi1.3v3, Raspberry_Pi1.3V3, DRV_1.RESET, DRV_1.SLEEP, DRV_2.RESET, DRV_2.SLEEP, DRV_3.RESET, DRV_3.SLEEP, DRV_4.RESET, DRV_4.SLEEP, DRV_5.RESET, DRV_5.SLEEP, DRV_6.RESET, DRV_6.SLEEP
  N1: Raspberry_Pi1.GPIO2, J1.pulse
  N2: Raspberry_Pi1.GIPO19, DRV_6.DIRECTION
  N3: Raspberry_Pi1.GIPO26, DRV_6.STEP
  GND: Raspberry_Pi1.GND, DRV_1.GROUND_LOG, DRV_2.GROUND_ST/_MT, DRV_2.GROUND_LOG, DRV_3.GROUND_ST/_MT, DRV_3.GROUND_LOG, DRV_4.GROUND_ST/_MT, DRV_4.GROUND_LOG, DRV_5.GROUND_ST/_MT, DRV_5.GROUND_LOG, DRV_6.GROUND_ST/_MT, DRV_6.GROUND_LOG, C1.-, C2.-, C3.-, C4.-, C5.-, C6.-, J1.gnd, U1.GND1, Power_plug1.GND
  N4: Raspberry_Pi1.GIPO21, DRV_1.STEP
  N5: Raspberry_Pi1.GIPO20, DRV_1.DIRECTION
  N6: Raspberry_Pi1.GIPO16, DRV_2.STEP
  N7: Raspberry_Pi1.GIPO12, DRV_2.DIRECTION
  N8: Raspberry_Pi1.ID_SC, DRV_3.STEP
  N9: Raspberry_Pi1.GIPO7, DRV_3.DIRECTION
  N10: Raspberry_Pi1.GIPO8, DRV_4.STEP
  N11: Raspberry_Pi1.GIPO25, DRV_4.DIRECTION
  N12: Raspberry_Pi1.GIPO24, DRV_5.STEP
  N13: Raspberry_Pi1.GIPO23, DRV_5.DIRECTION
  N14: Raspberry_Pi1.GIPO18, DRV_1.MS3, DRV_2.MS3, DRV_3.MS3, DRV_4.MS3, DRV_5.MS3, DRV_6.MS3
  N15: Raspberry_Pi1.GIPO15, DRV_1.MS2, DRV_2.MS2, DRV_3.MS2, DRV_4.MS2, DRV_5.MS2, DRV_6.MS2
  N16: Raspberry_Pi1.GIPO14, DRV_1.MS1, DRV_2.MS1, DRV_3.MS1, DRV_4.MS1, DRV_5.MS1, DRV_6.MS1
  N17: DRV_1.OUT_2B, M1.A, M2.C
  N18: DRV_1.OUT_2A, M1.C, M2.A
  N19: DRV_1.OUT_1A, M1.B, M2.D
  N20: DRV_1.OUT_1B, M1.D, M2.B
  N21: DRV_2.OUT_2B, M3.A
  N22: DRV_2.OUT_2A, M3.C
  N23: DRV_2.OUT_1A, M3.B
  N24: DRV_2.OUT_1B, M3.D
  VIN: DRV_3.VOLTAGE_ST/_MT, DRV_4.VOLTAGE_ST/_MT, DRV_5.VOLTAGE_ST/_MT, DRV_6.VOLTAGE_ST/_MT, C1.+, C2.+, C3.+, C4.+, C5.+, C6.+, U1.VIN, Power_plug1.VCC
  N25: DRV_3.OUT_2B, M7.A
  N26: DRV_3.OUT_2A, M7.C
  N27: DRV_3.OUT_1A, M7.B
  N28: DRV_3.OUT_1B, M7.D
  N29: DRV_4.OUT_2B, M4.A
  N30: DRV_4.OUT_2A, M4.C
  N31: DRV_4.OUT_1A, M4.B
  N32: DRV_4.OUT_1B, M4.D
  N33: DRV_5.OUT_2B, M5.A
  N34: DRV_5.OUT_2A, M5.C
  N35: DRV_5.OUT_1A, M5.B
  N36: DRV_5.OUT_1B, M5.D
  N37: DRV_6.OUT_2B, M6.A
  N38: DRV_6.OUT_2A, M6.C
  N39: DRV_6.OUT_1A, M6.B
  N40: DRV_6.OUT_1B, M6.D
  N41: J1.vcc, U1.VOUT
